# Fritzing sketch train_sound_box (saved by Fritzing 0.9.3b)
breadboards: 1

parts:
  SP1 = SPEAKER [package=pcb_mount_speaker]
  S2 = Pushbutton [package="[THT]"]
  S4 = Pushbutton [package="[THT]"]
  S3 = Pushbutton [package="[THT]"]
  S6 = Pushbutton [package="[THT]"]
  S5 = Pushbutton [package="[THT]"]
  S1 = Pushbutton [package="[THT]"]
  R2 = Resistor [tolerance=±5% resistance=2k package=THT]
  R1 = Resistor [tolerance=±5% resistance=1k package=THT]
  R3 = Resistor [tolerance=±5% resistance=3k package=THT]
  R4 = Resistor [tolerance=±5% resistance=5.1k package=THT]
  R5 = Resistor [tolerance=±5% resistance=6.8k package=THT]
  R6 = Resistor [tolerance=±5% resistance=10k package=THT]
  R7 = Resistor [tolerance=±5% resistance=100k package=THT]
  R8 = Resistor [tolerance=±5% resistance=10k package=THT]
  DFPlayer_Mini1 = DFPlayer MINI [package="DIP (Dual Inline) [THT]"]
  Onderdeel2 = Arduino Uno (Rev3)
  LCD2 = LCD screen
  LCM1602_IIC2 = LCM1602 IIC [part_number="LCM1602 IIC" chip_label="LCM1602 IIC" package="DIP (Dual Inline) [THT]"]

nets:
  N1: SP1.+, DFPlayer_Mini1.SPK2
  N2: SP1.-, DFPlayer_Mini1.SPK1
  N3: S2.Pin_1, S2.Pin_2, R2.Pin_1
  N4: S2.Pin_3, S2.Pin_4, S4.Pin_3, S4.Pin_4, S3.Pin_3, S3.Pin_4, S6.Pin_3, S6.Pin_4, S5.Pin_3, S5.Pin_4, S1.Pin_3, S1.Pin_4, R7.Pin_1, Onderdeel2.A0
  N5: S4.Pin_1, S4.Pin_2, R4.Pin_1
  N6: S3.Pin_1, S3.Pin_2, R3.Pin_1
  N7: S6.Pin_1, S6.Pin_2, R6.Pin_1
  N8: S5.Pin_1, S5.Pin_2, R5.Pin_1
  N9: S1.Pin_1, S1.Pin_2, R1.Pin_1
  VCC: R2.Pin_0, R1.Pin_0, R3.Pin_0, R4.Pin_0, R5.Pin_0, R6.Pin_0, DFPlayer_Mini1.VCC, Onderdeel2.5V, LCM1602_IIC2.VCC
  GND: R7.Pin_0, DFPlayer_Mini1.GND#6, Onderdeel2.GND, LCM1602_IIC2.GND
  N10: R8.Pin_0, DFPlayer_Mini1.RX
  N11: R8.Pin_1, Onderdeel2.D2
  N12: DFPlayer_Mini1.TX, Onderdeel2.D3_PWM
  N13: Onderdeel2.A4/SDA, LCM1602_IIC2.SDA
  N14: Onderdeel2.A5/SCL, LCM1602_IIC2.SCL
  VSS: LCD2.VSS, LCM1602_IIC2.VSS
  VDD: LCD2.VDD, LCM1602_IIC2.VDD
  N15: LCD2.V0, LCM1602_IIC2.V0
  N16: LCD2.RS, LCM1602_IIC2.RS
  N17: LCD2.R/W, LCM1602_IIC2.RW
  N18: LCD2.E, LCM1602_IIC2.E
  N19: LCD2.DB0, LCM1602_IIC2.D0
  N20: LCD2.DB1, LCM1602_IIC2.D1
  N21: LCD2.DB2, LCM1602_IIC2.D2
  N22: LCD2.DB3, LCM1602_IIC2.D3
  N23: LCD2.DB4, LCM1602_IIC2.D4
  N24: LCD2.DB5, LCM1602_IIC2.D5
  N25: LCD2.DB6, LCM1602_IIC2.D6
  N26: LCD2.DB7, LCM1602_IIC2.D7
  N27: LCD2.LED+, LCM1602_IIC2.A
  N28: LCD2.LED-, LCM1602_IIC2.K
  N29: LCM1602_IIC2.LED_A, LCM1602_IIC2.LED_B

custom parts:
  DFPlayer MINI: MP3 module by DFRobot.com for playing Music from an SD-Card. Supports WAV and MP3 files.
  LCM1602 IIC: I2C-Module to use a 1602 or 2004 LCD on with the wire.h libory Serial LCD Modul
